# Fritzing sketch Schematic (saved by Fritzing 0.9.3b)
breadboards: 1

parts:
  WS2812B = WS2812B
  C2 = Electrolytic Capacitor [capacitance=1000µF package="300 mil [THT, electrolytic]"]
  R1 = Resistor [tolerance=±5% resistance=480 package=THT]
  Adafruit_HUZZAH_ESP8266_Breakout1 = Adafruit HUZZAH ESP8266 Breakout [part_number=2471]
  FTDI = FTDI_BASIC [package=ftdi_basic]
  Part1 = Logic Level Converter
  V1 = DC Power [voltage=5]

nets:
  GND: WS2812B.GND, C2.-, Adafruit_HUZZAH_ESP8266_Breakout1.GND, FTDI.5, Part1.GND, V1.V-
  N1: WS2812B.Din, R1.Pin_1
  N2: WS2812B.+5V, C2.+, Adafruit_HUZZAH_ESP8266_Breakout1.V+#3, Part1.HV, V1.V+
  N3: R1.Pin_0, Part1.RX_HV
  N4: Adafruit_HUZZAH_ESP8266_Breakout1.#14, Part1.TX_LV
  N5: Adafruit_HUZZAH_ESP8266_Breakout1.TX, FTDI.3
  N6: Adafruit_HUZZAH_ESP8266_Breakout1.RX, FTDI.2
  N7: Adafruit_HUZZAH_ESP8266_Breakout1.3V, Part1.LV
  N8: Adafruit_HUZZAH_ESP8266_Breakout1.V+#22, FTDI.6

notes:
  WifiLights, 1
